# Fritzing sketch map (saved by Fritzing 0.9.3b)
circuit board: 8.46667cm x 5.64444cm
breadboards: 1

parts:
  VCC1 = Battery
  Part1 = Arduino Nano (Rev3.0)
  U1 = 3.5mm Audio Jack [package=audio-jack]
  LED1 = 7-SEGMENT-4DIGIT-YOUNGSUN [package=7-segment-4digit-youngsun]  # not connected

nets:
  N1: VCC1.-, Part1.GND, U1.SLEEVE
  N2: VCC1.+, Part1.VIN
  N3: Part1.A0, U1.RIGHT
